// Logisim project DLAssignment.circ as structural Verilog
// add1
module _19071110add1 (
  input  X,
  input  Y,
  input  Ci,
  output S,
  output Co
);

  wire and_1_out, and_2_out, xor_1_out;

  xor xor_1 (xor_1_out, X, Y);
  and and_1 (and_1_out, X, Y);
  and and_2 (and_2_out, xor_1_out, Ci);
  xor xor_2 (S, xor_1_out, Ci);
  or or_1 (Co, and_2_out, and_1_out);
endmodule

// add4
module _19071110add4 (
  input  [3:0] X,
  input  [3:0] Y,
  input  Ci,
  output [3:0] S,
  output Co
);

  wire n19071110add1_1_co, n19071110add1_2_co, n19071110add1_3_co;

  _19071110add1 u_19071110add1_1 (.X(X[0]), .Y(Y[0]), .Ci(Ci), .S(S[0]), .Co(n19071110add1_1_co));
  _19071110add1 u_19071110add1_2 (.X(X[1]), .Y(Y[1]), .Ci(n19071110add1_1_co), .S(S[1]), .Co(n19071110add1_2_co));
  _19071110add1 u_19071110add1_3 (.X(X[2]), .Y(Y[2]), .Ci(n19071110add1_2_co), .S(S[2]), .Co(n19071110add1_3_co));
  _19071110add1 u_19071110add1_4 (.X(X[3]), .Y(Y[3]), .Ci(n19071110add1_3_co), .S(S[3]), .Co(Co));
endmodule

// add32
module _19071110add32 (
  input  [31:0] X,
  input  [31:0] Y,
  input  Ci,
  output [31:0] S,
  output Co
);

  wire n19071110add4_1_co, n19071110add4_2_co, n19071110add4_3_co, n19071110add4_4_co, n19071110add4_5_co,
       n19071110add4_6_co, n19071110add4_7_co;

  _19071110add4 u_19071110add4_1 (.X(X[3:0]), .Y(Y[3:0]), .Ci(Ci), .S(S[3:0]), .Co(n19071110add4_1_co));
  _19071110add4 u_19071110add4_2 (.X(X[7:4]), .Y(Y[7:4]), .Ci(n19071110add4_1_co), .S(S[7:4]), .Co(n19071110add4_2_co));
  _19071110add4 u_19071110add4_3 (
    .X(X[11:8]), .Y(Y[11:8]), .Ci(n19071110add4_2_co), .S(S[11:8]), .Co(n19071110add4_3_co));
  _19071110add4 u_19071110add4_4 (
    .X(X[15:12]), .Y(Y[15:12]), .Ci(n19071110add4_3_co), .S(S[15:12]), .Co(n19071110add4_4_co));
  _19071110add4 u_19071110add4_5 (
    .X(X[19:16]), .Y(Y[19:16]), .Ci(n19071110add4_4_co), .S(S[19:16]), .Co(n19071110add4_5_co));
  _19071110add4 u_19071110add4_6 (
    .X(X[23:20]), .Y(Y[23:20]), .Ci(n19071110add4_5_co), .S(S[23:20]), .Co(n19071110add4_6_co));
  _19071110add4 u_19071110add4_7 (
    .X(X[27:24]), .Y(Y[27:24]), .Ci(n19071110add4_6_co), .S(S[27:24]), .Co(n19071110add4_7_co));
  _19071110add4 u_19071110add4_8 (.X(X[31:28]), .Y(Y[31:28]), .Ci(n19071110add4_7_co), .S(S[31:28]), .Co(Co));
endmodule

// sub32
module _19071110sub32 (
  input  [31:0] X,
  input  [31:0] Y,
  input  Bi,
  output [31:0] D,
  output Bo
);

  wire n19071110add32_1_co, not_2_out;
  wire [31:0] not_1_out;

  assign not_1_out = ~Y;  // NOT_Gate not_1, 32 bits wide
  not not_2 (not_2_out, Bi);
  _19071110add32 u_19071110add32_1 (.X(X), .Y(not_1_out), .Ci(not_2_out), .S(D), .Co(n19071110add32_1_co));
  not not_3 (Bo, n19071110add32_1_co);
endmodule

// zero32
module _19071110isZero32 (
  input  [31:0] X,
  output zero
);

  nor nor_1 (zero, X[0], X[1], X[2], X[3], X[4], X[5], X[6], X[7], X[8], X[9], X[10], X[11], X[12], X[13], X[14], X[15], X[17], X[18], X[19], X[20], X[21], X[22], X[23], X[24], X[25], X[26], X[27], X[28], X[29], X[30], X[31], X[16]);
endmodule

// ALU-19071110
module _19071110ALU (
  input  [31:0] A,
  input  [31:0] B,
  input  [1:0] ALU_sel,
  output [31:0] ALU_out,
  output zero
);

  wire [31:0] and_1_out, n19071110add32_1_s, n19071110sub32_1_d, or_1_out;

  _19071110add32 u_19071110add32_1 (.X(A), .Y(B), .Ci(1'b0), .S(n19071110add32_1_s));  // open: Co
  _19071110sub32 u_19071110sub32_1 (.X(A), .Y(B), .Bi(1'b0), .D(n19071110sub32_1_d));  // open: Bo
  assign and_1_out = B & A;  // AND_Gate and_1, 32 bits wide
  assign or_1_out = B | A;  // OR_Gate or_1, 32 bits wide
  _19071110isZero32 u_19071110iszero32_1 (.X(ALU_out), .zero(zero));
  Multiplexer #(.select(2), .width(32), .disabled(0), .enable("false")) multiplexer_1 (
    .in0(n19071110add32_1_s), .in1(n19071110sub32_1_d), .in2(and_1_out), .in3(or_1_out), .out(ALU_out),
    .sel(ALU_sel));
endmodule

// num-19071110
module _19071110num (
  input  [15:0] Imm16,
  input  [1:0] Extsel,
  output [31:0] ExtImm32
);

  wire bitselector_1_out;
  wire [15:0] multiplexer_1_out, not_1_out;

  assign not_1_out = ~{16{1'b0}};  // NOT_Gate not_1, 16 bits wide
  BitSelector #(.width(16)) bitselector_1 (.in(Imm16), .out(bitselector_1_out), .sel(4'b1111));
  Multiplexer #(.width(16), .disabled(0), .enable("false")) multiplexer_1 (
    .in0({16{1'b0}}), .in1(not_1_out), .out(multiplexer_1_out), .sel(bitselector_1_out));
  Multiplexer #(.select(2), .width(32), .disabled(0), .enable("false")) multiplexer_2 (
    .in0({{16{1'b0}}, Imm16}), .in1({multiplexer_1_out, Imm16}), .in2({Imm16, {16{1'b0}}}), .out(ExtImm32),
    .sel(Extsel));  // open: in3
endmodule

// Mdec-19071110
module _19071110Mdec (
  input  [5:0] opcode,
  input  [5:0] funct,
  output addu,
  output subu,
  output ori,
  output lui,
  output lw,
  output sw,
  output beq
);

  wire and_1_out, and_2_out, and_3_out, nor_1_out;

  and and_1 (and_1_out, funct[0], ~funct[2], ~funct[3], ~funct[4], funct[5]);  // AND_Gate
  and and_2 (and_2_out, opcode[0], opcode[2], opcode[3], ~opcode[4], ~opcode[5]);  // AND_Gate
  and and_3 (and_3_out, opcode[0], opcode[1], ~opcode[2], ~opcode[4], opcode[5]);  // AND_Gate
  and and_4 (beq, ~opcode[0], ~opcode[1], opcode[2], ~opcode[3], ~opcode[4], ~opcode[5]);  // AND_Gate
  nor nor_1 (nor_1_out, opcode[0], opcode[1], opcode[2], opcode[3], opcode[4], opcode[5]);
  and and_5 (addu, ~funct[1], and_1_out, nor_1_out);  // AND_Gate
  and and_6 (subu, nor_1_out, and_1_out, funct[1]);
  and and_7 (ori, ~opcode[1], and_2_out);  // AND_Gate
  and and_8 (lui, and_2_out, opcode[1]);
  and and_9 (lw, ~opcode[3], and_3_out);  // AND_Gate
  and and_10 (sw, and_3_out, opcode[3]);
endmodule

// Mcod-19071110
module _19071110Mcod (
  input  addu,
  input  subu,
  input  ori,
  input  lui,
  input  lw,
  input  sw,
  input  beq,
  input  zero,
  output [1:0] ALU_sel,
  output [1:0] EXT_sel,
  output B_sel,
  output PC_sel
);

  wire and_1_out, and_2_out, priority_encoder_1_gs;
  wire [2:0] priority_encoder_1_out;

  and and_1 (and_1_out, beq, ~zero);  // AND_Gate
  and and_2 (and_2_out, beq, zero);
  Priority_Encoder priority_encoder_1 (
    .in0(addu), .in1(subu), .in2(ori), .in3(lui), .in4(lw), .in5(sw), .in6(and_1_out), .in7(and_2_out),
    .out(priority_encoder_1_out), .gs(priority_encoder_1_gs));  // open: en_in, en_out
  Multiplexer #(.select(3), .width(6), .disabled(0)) multiplexer_1 (
    .in0({6{1'b0}}), .in1(6'b010000), .in2(6'b110010), .in3(6'b001010), .in4(6'b000110), .in5(6'b000110),
    .in6(6'b010000), .in7(6'b010001), .out({ALU_sel, EXT_sel, B_sel, PC_sel}), .sel(priority_encoder_1_out),
    .en(priority_encoder_1_gs));
endmodule

// main-19071110
module _19071110main (
  input  [5:0] opcode,
  input  [5:0] funct,
  input  [31:0] A,
  input  [31:0] B,
  input  [15:0] Imm16,
  output PC_sel,
  output [31:0] ALU_out,
  output zero
);

  wire n19071110mcod_1_b_sel, n19071110mdec_1_addu, n19071110mdec_1_beq, n19071110mdec_1_lui,
       n19071110mdec_1_lw, n19071110mdec_1_ori, n19071110mdec_1_subu, n19071110mdec_1_sw;
  wire [1:0] n19071110mcod_1_alu_sel, n19071110mcod_1_ext_sel;
  wire [31:0] multiplexer_1_out, n19071110num_1_extimm32;

  _19071110Mdec u_19071110mdec_1 (
    .opcode(opcode), .funct(funct), .addu(n19071110mdec_1_addu), .subu(n19071110mdec_1_subu),
    .ori(n19071110mdec_1_ori), .lui(n19071110mdec_1_lui), .lw(n19071110mdec_1_lw), .sw(n19071110mdec_1_sw),
    .beq(n19071110mdec_1_beq));
  _19071110num u_19071110num_1 (.Imm16(Imm16), .Extsel(n19071110mcod_1_ext_sel), .ExtImm32(n19071110num_1_extimm32));
  _19071110Mcod u_19071110mcod_1 (
    .addu(n19071110mdec_1_addu), .subu(n19071110mdec_1_subu), .ori(n19071110mdec_1_ori),
    .lui(n19071110mdec_1_lui), .lw(n19071110mdec_1_lw), .sw(n19071110mdec_1_sw), .beq(n19071110mdec_1_beq),
    .zero(zero), .ALU_sel(n19071110mcod_1_alu_sel), .EXT_sel(n19071110mcod_1_ext_sel),
    .B_sel(n19071110mcod_1_b_sel), .PC_sel(PC_sel));
  Multiplexer #(.width(32), .disabled(0), .enable("false")) multiplexer_1 (
    .in0(B), .in1(n19071110num_1_extimm32), .out(multiplexer_1_out), .sel(n19071110mcod_1_b_sel));
  _19071110ALU u_19071110alu_1 (
    .A(A), .B(multiplexer_1_out), .ALU_sel(n19071110mcod_1_alu_sel), .ALU_out(ALU_out), .zero(zero));
endmodule
