// Logisim project PCOAssignment.circ as structural Verilog: 17 circuits, main circuit 19071110ALU
module _19071110main (
  input  reset
);

  wire AddrError, addu, ALUSrc, beq, clk_out, InvalidInstrError, j, lui, lw, Mem2Reg, MemWrite, ori, RegDst,
       RegWrite, subu, sw, zero;
  wire [1:0] ALUOp, ExtOp, NPCSel;
  wire [2:0] CommandID;
  wire [4:0] RegDstID;
  wire [25:0] addr26;
  wire [31:0] A, ALUIn, ALUOut, B, Ext, RAMOut, RegWriteData;
  wire [31:26] Instr;

  // Probe on NPCSel
  // Probe on {Instr, addr26}
  Decoder #(.select(3), .tristate("false"), .disabled("Z"), .enable("false")) decoder_1 (
    .out0(addu), .out1(subu), .out2(ori), .out3(lw), .out4(sw), .out5(beq), .out6(lui), .out7(j),
    .sel(CommandID));
  Clock #(.highDuration(1), .lowDuration(1)) clk (.out(clk_out));
  // Probe on Instr
  // Probe on InvalidInstrError
  _19071110IFU u_19071110ifu_1 (
    .IfBeq(NPCSel[0]), .IfJmp(NPCSel[1]), .BeqAddr(addr26[15:0]), .JmpAddr(addr26), .reset(reset),
    .clk(clk_out), .Instruction({Instr, addr26}));
  // Probe on A
  // Probe on ExtOp
  // Probe on ALUSrc
  // Probe on Ext
  // Probe on B
  // Probe on ALUIn
  // Probe on addr26[5:0]
  // Probe on addr26[15:11]
  // Probe on addr26[20:16]
  // Probe on addr26[25:21]
  _19071110GPR u_19071110gpr_1 (
    .AddrWrite(RegDstID), .Din(RegWriteData), .WE(RegWrite), .clear(reset), .preset(1'b0),
    .AddrRead1(addr26[25:21]), .RD1(A), .AddrRead2(addr26[20:16]), .RD2(B), .clk(clk_out));
  Multiplexer #(.select(1), .width(5), .disabled("Z"), .enable("false")) multiplexer_1 (
    .in0(addr26[20:16]), .in1(addr26[15:11]), .out(RegDstID), .sel(RegDst));
  // Probe on A
  // Probe on ALUOp
  // Probe on ALUOut
  _19071110Controller u_19071110controller_1 (
    .Funct(addr26[5:0]), .OpCode(Instr), .ErrorInvalidInput(InvalidInstrError), .RegDst(RegDst),
    .ALUSrc(ALUSrc), .Mem2Reg(Mem2Reg), .RegWrite(RegWrite), .MemWrite(MemWrite), .NPCSel(NPCSel),
    .ExtOp(ExtOp), .ALUOP(ALUOp), .IsZero(zero), .CommandID(CommandID));
  _19071110Extender u_19071110extender_1 (.imm16(addr26[15:0]), .ExtOP(ExtOp), .ext32(Ext));
  // Probe on ALUIn
  // Probe on Instr
  // Probe on addr26[20:16]
  Multiplexer #(.select(1), .width(32), .disabled("Z"), .enable("false")) multiplexer_2 (
    .in0(B), .in1(Ext), .out(ALUIn), .sel(ALUSrc));
  Multiplexer #(.select(1), .width(32), .disabled("Z"), .enable("false")) multiplexer_3 (
    .in0(ALUOut), .in1(RAMOut), .out(RegWriteData), .sel(Mem2Reg));
  // Probe on MemWrite
  // Probe on AddrError
  // Probe on zero
  // Probe on addr26[15:0]
  // Probe on addr26[25:21]
  _19071110ALU u_19071110alu_1 (.A(A), .B(ALUIn), .ALUOp(ALUOp), .out(ALUOut), .out_5(zero));
  // Probe on AddrError
  _19071110RAM u_19071110ram_1 (
    .Din(B), .addr(ALUOut), .addrError(AddrError), .Dout(RAMOut), .clr(reset), .WE(MemWrite), .clk(clk_out));
  // Probe on Mem2Reg
  // Probe on RegWriteData
  // Probe on RegDst
  // Probe on RegDstID
  // Probe on ALUOut
  // Probe on RAMOut
  // Probe on RegWrite
  // Probe on Instr
  // Probe on addr26

  // Other names for the same wires on the sheet: funct[5:0] = addr26[5:0]; imm16[15:0] = addr26[15:0];
  //   Instr[25:0] = addr26; rd[4:0] = addr26[15:11]; rt[4:0] = addr26[20:16]; rs[4:0] = addr26[25:21];
  //   opcode[5:0] = Instr

  // Notes on the sheet:
  //   1. 取指IF
  //   00=PC+4, 01=beq, 10=j
  //   opcode
  //   addr26
  //   0=B, 1=Ext
  //   2. 译码/寄存器读ID
  //   00=zero, 01=sign, 10=lui
  //   R type: $                               ,        ,
  //   GPR[rd] <- GPR[rs] + GPR[rt]
  //   GPR[rd] <- GPR[rs] - GPR[rt]
  //   func
  //   shmat
  //   imm16
  //   3. 执行EX
  //   00=and, 01=sub, 10=and, 11=or
  //   I type: $                              ,       ,
  //   GPR[rt] <- GPR[rs] or immediate
  //   if GPR[rs] = GPR[rt] then branch
  //   GPR[rt] <- immediate || 0^16
  //   4. 访存MEM
  //   (offset)
  //   (base)
  //   GPR[rt] <- memory[GPR[base] + offset]
  //   memory[GPR[base] + offset] <- GPR[rt]
  //   5. 寄存器写回WB
  //   0=rt, 1=rd
  //   J type: $ 
  //   0=ALUOut, 1=RAM
  //   branch
endmodule

// Controller
module _19071110Controller (
  input  [5:0] Funct,
  input  [5:0] OpCode,
  input  IsZero,
  output ErrorInvalidInput,
  output RegDst,
  output ALUSrc,
  output Mem2Reg,
  output RegWrite,
  output MemWrite,
  output [1:0] NPCSel,
  output [1:0] ExtOp,
  output [1:0] ALUOP,
  output [2:0] CommandID
);

  wire addu_out, beq_out, j_out, lui_out, lw_out, ori_out, R_Instr_out, subu_out, sw_out;
  wire [10:0] n19071110signalcollector_1_signals, n19071110signalcollector_2_signals,
       n19071110signalcollector_3_signals, n19071110signalcollector_4_signals,
       n19071110signalcollector_5_signals, n19071110signalcollector_6_signals,
       n19071110signalcollector_7_signals, n19071110signalcollector_8_signals;

  and R_Instr (R_Instr_out, ~OpCode[5], ~OpCode[4], ~OpCode[3], ~OpCode[2], ~OpCode[1], ~OpCode[0]);  // AND_Gate
  and addu (addu_out, R_Instr_out, Funct[5], ~Funct[4], ~Funct[3], ~Funct[2], ~Funct[1], Funct[0]);  // AND_Gate
  and subu (subu_out, R_Instr_out, Funct[5], ~Funct[4], ~Funct[3], ~Funct[2], Funct[1], Funct[0]);  // AND_Gate
  and ori (ori_out, ~OpCode[5], ~OpCode[4], OpCode[3], OpCode[2], ~OpCode[1], OpCode[0]);  // AND_Gate
  and lw (lw_out, OpCode[5], ~OpCode[4], ~OpCode[3], ~OpCode[2], OpCode[1], OpCode[0]);  // AND_Gate
  and sw (sw_out, OpCode[5], ~OpCode[4], OpCode[3], ~OpCode[2], OpCode[1], OpCode[0]);  // AND_Gate
  and beq (beq_out, ~OpCode[5], ~OpCode[4], ~OpCode[3], OpCode[2], ~OpCode[1], ~OpCode[0]);  // AND_Gate
  and lui (lui_out, ~OpCode[5], ~OpCode[4], OpCode[3], OpCode[2], OpCode[1], OpCode[0]);  // AND_Gate
  and j (j_out, ~OpCode[5], ~OpCode[4], ~OpCode[3], ~OpCode[2], OpCode[1], ~OpCode[0]);  // AND_Gate
  Priority_Encoder #(.select(3), .disabled("Z")) priority_encoder_1 (
    .in0(addu_out), .in1(subu_out), .in2(ori_out), .in3(lw_out), .in4(sw_out), .in5(beq_out), .in6(lui_out),
    .in7(j_out), .out(CommandID), .en_out(ErrorInvalidInput));  // open: gs, en_in
  _19071110SignalCollector u_19071110signalcollector_1 (
    .signals(n19071110signalcollector_1_signals), .RegDst(1'b1), .ALUSrc(1'b0), .Mem2Reg(1'b0),
    .RegWrite(1'b1), .MemWrite(1'b0), .NPCSel(2'b00), .ALUOp(2'b00));  // open: ExtOp
  _19071110SignalCollector u_19071110signalcollector_2 (
    .signals(n19071110signalcollector_2_signals), .RegDst(1'b1), .ALUSrc(1'b0), .Mem2Reg(1'b0),
    .RegWrite(1'b1), .MemWrite(1'b0), .NPCSel(2'b00), .ALUOp(2'b01));  // open: ExtOp
  _19071110SignalCollector u_19071110signalcollector_3 (
    .signals(n19071110signalcollector_3_signals), .RegDst(1'b0), .ALUSrc(1'b1), .Mem2Reg(1'b0),
    .RegWrite(1'b1), .MemWrite(1'b0), .NPCSel(2'b00), .ExtOp(2'b00), .ALUOp(2'b11));
  _19071110SignalCollector u_19071110signalcollector_4 (
    .signals(n19071110signalcollector_4_signals), .RegDst(1'b0), .ALUSrc(1'b1), .Mem2Reg(1'b1),
    .RegWrite(1'b1), .MemWrite(1'b0), .NPCSel(2'b00), .ExtOp(2'b01), .ALUOp(2'b00));
  _19071110SignalCollector u_19071110signalcollector_5 (
    .signals(n19071110signalcollector_5_signals), .RegDst(1'b0), .ALUSrc(1'b1), .Mem2Reg(1'b1),
    .RegWrite(1'b0), .MemWrite(1'b1), .NPCSel(2'b00), .ExtOp(2'b01), .ALUOp(2'b00));
  _19071110SignalCollector u_19071110signalcollector_6 (
    .signals(n19071110signalcollector_6_signals), .RegDst(1'b0), .ALUSrc(1'b0), .RegWrite(1'b0),
    .MemWrite(1'b0), .NPCSel({1'b0, IsZero}), .ALUOp(2'b01));  // open: Mem2Reg, ExtOp
  _19071110SignalCollector u_19071110signalcollector_7 (
    .signals(n19071110signalcollector_7_signals), .RegDst(1'b0), .ALUSrc(1'b1), .Mem2Reg(1'b0),
    .RegWrite(1'b1), .MemWrite(1'b0), .NPCSel(2'b00), .ExtOp(2'b10), .ALUOp(2'b11));
  _19071110SignalCollector u_19071110signalcollector_8 (
    .signals(n19071110signalcollector_8_signals), .RegWrite(1'b0), .MemWrite(1'b0), .NPCSel(2'b10));  // open: RegDst, ALUSrc, Mem2Reg, ExtOp, ALUOp
  Multiplexer #(.select(3), .width(11), .disabled("Z"), .enable("false")) multiplexer_1 (
    .in0(n19071110signalcollector_1_signals), .in1(n19071110signalcollector_2_signals),
    .in2(n19071110signalcollector_3_signals), .in3(n19071110signalcollector_4_signals),
    .in4(n19071110signalcollector_5_signals), .in5(n19071110signalcollector_6_signals),
    .in6(n19071110signalcollector_7_signals), .in7(n19071110signalcollector_8_signals),
    .out({RegDst, ALUSrc, Mem2Reg, RegWrite, MemWrite, NPCSel, ExtOp, ALUOP}), .sel(CommandID));

  // Notes on the sheet:
  //   0=B, 1=Ext
  //   0=ALU, 1=RAM
  //   0=PC+4, 1=beq, 2=jmp
  //   0=0-ext, 1=sign-ext
  //   0=add, 1=sub, 2=and, 3=or
endmodule

module _19071110SignalCollector (
  input  RegDst,
  input  ALUSrc,
  input  Mem2Reg,
  input  RegWrite,
  input  MemWrite,
  input  [1:0] NPCSel,
  input  [1:0] ExtOp,
  input  [1:0] ALUOp,
  output [10:0] signals
);


  assign signals = {RegDst, ALUSrc, Mem2Reg, RegWrite, MemWrite, NPCSel, ExtOp, ALUOp};
endmodule

// EXT
module _19071110Extender (
  input  [1:0] ExtOP,
  input  [15:0] imm16,
  output [31:0] ext32
);

  wire [31:0] bit_extender_1_out, bit_extender_2_out;

  assign bit_extender_1_out = {{16{1'b0}}, imm16};  // Bit_Extender bit_extender_1
  assign bit_extender_2_out = {{16{imm16[15]}}, imm16};  // Bit_Extender bit_extender_2
  Multiplexer #(.select(2), .width(32), .disabled("Z"), .enable("false")) multiplexer_1 (
    .in0(bit_extender_1_out), .in1(bit_extender_2_out), .in2({imm16, {16{1'b0}}}), .out(ext32), .sel(ExtOP));  // open: in3
endmodule

// RAM
module _19071110RAM (
  input  [31:0] Din,
  input  WE,
  input  [31:0] addr,
  input  clr,
  input  clk,
  output addrError,
  output [31:0] Dout
);

  wire not_1_out;

  or or_1 (addrError, addr[0], addr[1]);
  not not_1 (not_1_out, WE);
  RAM #(.addrWidth(8), .dataWidth(8), .bus("combined"), .Select("low")) ram_1 (
    .addr(addr[9:2]), .data(Dout[7:0]), .clk(clk), .ld(not_1_out), .clr(clr));  // open: sel
  RAM #(.addrWidth(8), .dataWidth(8), .bus("combined"), .Select("low")) ram_2 (
    .addr(addr[9:2]), .data(Dout[15:8]), .clk(clk), .ld(not_1_out), .clr(clr));  // open: sel
  RAM #(.addrWidth(8), .dataWidth(8), .bus("combined"), .Select("low")) ram_3 (
    .addr(addr[9:2]), .data(Dout[23:16]), .clk(clk), .ld(not_1_out), .clr(clr));  // open: sel
  RAM #(.addrWidth(8), .dataWidth(8), .bus("combined"), .Select("low")) ram_4 (
    .addr(addr[9:2]), .data(Dout[31:24]), .clk(clk), .ld(not_1_out), .clr(clr));  // open: sel
  Multiplexer #(.select(1), .width(32), .disabled("Z"), .enable("false")) multiplexer_1 (
    .in0(Din), .out(Dout), .sel(not_1_out));  // open: in1
endmodule

// IFU
module _19071110IFU (
  input  IfBeq,
  input  IfJmp,
  input  [15:0] BeqAddr,
  input  [25:0] JmpAddr,
  input  reset,
  input  clk,
  output [31:0] Instruction
);

  wire [1:0] priority_encoder_1_out;
  wire [31:0] adder_1_out, adder_2_out, bit_extender_1_out, multiplexer_1_out, multiplexer_2_out,
       register_1_q, shifter_1_out;

  assign bit_extender_1_out = {{16{BeqAddr[15]}}, BeqAddr};  // Bit_Extender bit_extender_1
  Shifter #(.width(32), .shift("ll")) shifter_1 (.in(bit_extender_1_out), .\dist (5'b00010), .out(shifter_1_out));
  Adder #(.width(32)) adder_1 (.a(shifter_1_out), .b(adder_2_out), .out(adder_1_out));  // open: cin, cout
  Priority_Encoder #(.select(2), .disabled("Z")) priority_encoder_1 (
    .in0(1'b1), .in2(IfJmp), .in3(IfBeq), .out(priority_encoder_1_out), .en_in(1'b1));  // open: in1, gs, en_out
  Multiplexer #(.select(2), .width(32), .disabled("Z"), .enable("false")) multiplexer_1 (
    .in0(adder_2_out), .in2({adder_2_out[31:28], JmpAddr, adder_2_out[1:0]}), .in3(adder_1_out),
    .out(multiplexer_1_out), .sel(priority_encoder_1_out));  // open: in1
  Multiplexer #(.select(1), .width(32), .disabled("Z"), .enable("false")) multiplexer_2 (
    .in0(multiplexer_1_out), .in1(32'h3000), .out(multiplexer_2_out), .sel(reset));
  Register #(.width(32), .trigger("rising"), .Select("low")) register_1 (
    .D(multiplexer_2_out), .en(1'b1), .Q(register_1_q), .clk(clk));  // open: clr
  Adder #(.width(32)) adder_2 (.a(register_1_q), .b(32'h4), .out(adder_2_out));  // open: cin, cout
  ROM #(.addrWidth(8), .dataWidth(8), .Select("low")) ROM_0 (.addr(register_1_q[9:2]), .data(Instruction[31:24]));
  ROM #(.addrWidth(8), .dataWidth(8), .Select("low")) ROM_1 (.addr(register_1_q[9:2]), .data(Instruction[23:16]));
  ROM #(.addrWidth(8), .dataWidth(8), .Select("low")) ROM_2 (.addr(register_1_q[9:2]), .data(Instruction[15:8]));
  ROM #(.addrWidth(8), .dataWidth(8), .Select("low")) ROM_3 (.addr(register_1_q[9:2]), .data(Instruction[7:0]));

  // Notes on the sheet:
  //   contents of ROM_0 (hex, n*v repeats v):
  //   34 34 0 0 1 ac 8c 11 3c 8 34 3c 8 3c 8 34 3c 8
  //   contents of ROM_1 (hex, n*v repeats v):
  //   3 6 66 66 2a 9 a 2a b 0 b 9 0 b 10 b 9 10
  //   contents of ROM_2 (hex, n*v repeats v):
  //   0 0 40 48 4*0 cd c ef 45 c 45
  //   contents of ROM_3 (hex, n*v repeats v):
  //   93 ae 21 23 21 10 10 2 cd d ef 67 7 cd d ef 67 7
endmodule

// GPR
module _19071110GPR (
  input  clk,
  input  clear,
  input  [4:0] AddrWrite,
  input  [31:0] Din,
  input  [4:0] AddrRead1,
  input  [4:0] AddrRead2,
  input  preset,
  input  WE,
  output [31:0] RD1,
  output [31:0] RD2
);

  wire demultiplexer_1_out1, demultiplexer_1_out2, demultiplexer_1_out3, demultiplexer_1_out4,
       demultiplexer_1_out5, demultiplexer_1_out6, demultiplexer_1_out7, demultiplexer_1_out8,
       demultiplexer_1_out9, demultiplexer_1_out10, demultiplexer_1_out11, demultiplexer_1_out12,
       demultiplexer_1_out13, demultiplexer_1_out14, demultiplexer_1_out15, demultiplexer_1_out16,
       demultiplexer_1_out17, demultiplexer_1_out18, demultiplexer_1_out19, demultiplexer_1_out20,
       demultiplexer_1_out21, demultiplexer_1_out22, demultiplexer_1_out23, demultiplexer_1_out24,
       demultiplexer_1_out25, demultiplexer_1_out26, demultiplexer_1_out27, demultiplexer_1_out28,
       demultiplexer_1_out29, demultiplexer_1_out30, demultiplexer_1_out31;
  wire [31:0] Reg0, Reg1, Reg2, Reg3, Reg4, Reg5, Reg6, Reg7, Reg8, Reg9, Reg10, Reg11, Reg12, Reg13, Reg14,
       Reg15, register_1_q, register_2_q, register_3_q, register_4_q, register_5_q, register_6_q,
       register_7_q, register_8_q, register_9_q, register_10_q, register_11_q, register_12_q, register_13_q,
       register_14_q, register_15_q, register_16_q;

  Demultiplexer #(.select(5), .width(1), .tristate("false"), .disabled("Z"), .enable("false")) demultiplexer_1 (
    .out1(demultiplexer_1_out1), .out2(demultiplexer_1_out2), .out3(demultiplexer_1_out3),
    .out4(demultiplexer_1_out4), .out5(demultiplexer_1_out5), .out6(demultiplexer_1_out6),
    .out7(demultiplexer_1_out7), .out8(demultiplexer_1_out8), .out9(demultiplexer_1_out9),
    .out10(demultiplexer_1_out10), .out11(demultiplexer_1_out11), .out12(demultiplexer_1_out12),
    .out13(demultiplexer_1_out13), .out14(demultiplexer_1_out14), .out15(demultiplexer_1_out15),
    .out16(demultiplexer_1_out16), .out17(demultiplexer_1_out17), .out18(demultiplexer_1_out18),
    .out19(demultiplexer_1_out19), .out20(demultiplexer_1_out20), .out21(demultiplexer_1_out21),
    .out22(demultiplexer_1_out22), .out23(demultiplexer_1_out23), .out24(demultiplexer_1_out24),
    .out25(demultiplexer_1_out25), .out26(demultiplexer_1_out26), .out27(demultiplexer_1_out27),
    .out28(demultiplexer_1_out28), .out29(demultiplexer_1_out29), .out30(demultiplexer_1_out30),
    .out31(demultiplexer_1_out31), .in(WE), .sel(AddrWrite));  // open: out0
  Register #(.width(32), .trigger("rising"), .Select("low")) register_1 (
    .D(Din), .en(demultiplexer_1_out31), .Q(register_1_q), .clk(clk), .clr(clear), .cs(1'b0), .preset(preset));
  Register #(.width(32), .trigger("rising"), .Select("low")) register_2 (
    .D(Din), .en(demultiplexer_1_out30), .Q(register_2_q), .clk(clk), .clr(clear), .cs(1'b0), .preset(preset));
  Register #(.width(32), .trigger("rising"), .Select("low")) register_3 (
    .D(Din), .en(demultiplexer_1_out29), .Q(register_3_q), .clk(clk), .clr(clear), .cs(1'b0), .preset(preset));
  Register #(.width(32), .trigger("rising"), .Select("low")) register_4 (
    .D(Din), .en(demultiplexer_1_out28), .Q(register_4_q), .clk(clk), .clr(clear), .cs(1'b0), .preset(preset));
  Register #(.width(32), .trigger("rising"), .Select("low")) register_5 (
    .D(Din), .en(demultiplexer_1_out27), .Q(register_5_q), .clk(clk), .clr(clear), .cs(1'b0), .preset(preset));
  Register #(.width(32), .trigger("rising"), .Select("low")) register_6 (
    .D(Din), .en(demultiplexer_1_out26), .Q(register_6_q), .clk(clk), .clr(clear), .cs(1'b0), .preset(preset));
  Register #(.width(32), .trigger("rising"), .Select("low")) register_7 (
    .D(Din), .en(demultiplexer_1_out25), .Q(register_7_q), .clk(clk), .clr(clear), .cs(1'b0), .preset(preset));
  Register #(.width(32), .trigger("rising"), .Select("low")) register_8 (
    .D(Din), .en(demultiplexer_1_out24), .Q(register_8_q), .clk(clk), .clr(clear), .cs(1'b0), .preset(preset));
  Register #(.width(32), .trigger("rising"), .Select("low")) register_9 (
    .D(Din), .en(demultiplexer_1_out23), .Q(register_9_q), .clk(clk), .clr(clear), .cs(1'b0), .preset(preset));
  Register #(.width(32), .trigger("rising"), .Select("low")) register_10 (
    .D(Din), .en(demultiplexer_1_out22), .Q(register_10_q), .clk(clk), .clr(clear), .cs(1'b0), .preset(preset));
  Register #(.width(32), .trigger("rising"), .Select("low")) register_11 (
    .D(Din), .en(demultiplexer_1_out21), .Q(register_11_q), .clk(clk), .clr(clear), .cs(1'b0), .preset(preset));
  Register #(.width(32), .trigger("rising"), .Select("low")) register_12 (
    .D(Din), .en(demultiplexer_1_out20), .Q(register_12_q), .clk(clk), .clr(clear), .cs(1'b0), .preset(preset));
  Register #(.width(32), .trigger("rising"), .Select("low")) register_13 (
    .D(Din), .en(demultiplexer_1_out19), .Q(register_13_q), .clk(clk), .clr(clear), .cs(1'b0), .preset(preset));
  Register #(.width(32), .trigger("rising"), .Select("low")) register_14 (
    .D(Din), .en(demultiplexer_1_out18), .Q(register_14_q), .clk(clk), .clr(clear), .cs(1'b0), .preset(preset));
  Register #(.width(32), .trigger("rising"), .Select("low")) register_15 (
    .D(Din), .en(demultiplexer_1_out17), .Q(register_15_q), .clk(clk), .clr(clear), .cs(1'b0), .preset(preset));
  Register #(.width(32), .trigger("rising"), .Select("low")) register_16 (
    .D(Din), .en(demultiplexer_1_out16), .Q(register_16_q), .clk(clk), .clr(clear), .cs(1'b0), .preset(preset));
  Register #(.width(32), .trigger("rising"), .Select("low")) register_17 (
    .D(Din), .en(demultiplexer_1_out15), .Q(Reg15), .clk(clk), .clr(clear), .cs(1'b0), .preset(preset));
  Register #(.width(32), .trigger("rising"), .Select("low")) register_18 (
    .D(Din), .en(demultiplexer_1_out14), .Q(Reg14), .clk(clk), .clr(clear), .cs(1'b0), .preset(preset));
  Register #(.width(32), .trigger("rising"), .Select("low")) register_19 (
    .D(Din), .en(demultiplexer_1_out13), .Q(Reg13), .clk(clk), .clr(clear), .cs(1'b0), .preset(preset));
  Register #(.width(32), .trigger("rising"), .Select("low")) register_20 (
    .D(Din), .en(demultiplexer_1_out12), .Q(Reg12), .clk(clk), .clr(clear), .cs(1'b0), .preset(preset));
  Register #(.width(32), .trigger("rising"), .Select("low")) register_21 (
    .D(Din), .en(demultiplexer_1_out11), .Q(Reg11), .clk(clk), .clr(clear), .cs(1'b0), .preset(preset));
  Register #(.width(32), .trigger("rising"), .Select("low")) register_22 (
    .D(Din), .en(demultiplexer_1_out10), .Q(Reg10), .clk(clk), .clr(clear), .cs(1'b0), .preset(preset));
  Register #(.width(32), .trigger("rising"), .Select("low")) register_23 (
    .D(Din), .en(demultiplexer_1_out9), .Q(Reg9), .clk(clk), .clr(clear), .cs(1'b0), .preset(preset));
  Register #(.width(32), .trigger("rising"), .Select("low")) register_24 (
    .D(Din), .en(demultiplexer_1_out8), .Q(Reg8), .clk(clk), .clr(clear), .cs(1'b0), .preset(preset));
  Register #(.width(32), .trigger("rising"), .Select("low")) register_25 (
    .D(Din), .en(demultiplexer_1_out7), .Q(Reg7), .clk(clk), .clr(clear), .cs(1'b0), .preset(preset));
  Register #(.width(32), .trigger("rising"), .Select("low")) register_26 (
    .D(Din), .en(demultiplexer_1_out6), .Q(Reg6), .clk(clk), .clr(clear), .cs(1'b0), .preset(preset));
  Register #(.width(32), .trigger("rising"), .Select("low")) register_27 (
    .D(Din), .en(demultiplexer_1_out5), .Q(Reg5), .clk(clk), .clr(clear), .cs(1'b0), .preset(preset));
  Register #(.width(32), .trigger("rising"), .Select("low")) register_28 (
    .D(Din), .en(demultiplexer_1_out4), .Q(Reg4), .clk(clk), .clr(clear), .cs(1'b0), .preset(preset));
  Register #(.width(32), .trigger("rising"), .Select("low")) register_29 (
    .D(Din), .en(demultiplexer_1_out3), .Q(Reg3), .clk(clk), .clr(clear), .cs(1'b0), .preset(preset));
  Register #(.width(32), .trigger("rising"), .Select("low")) register_30 (
    .D(Din), .en(demultiplexer_1_out2), .Q(Reg2), .clk(clk), .clr(clear), .cs(1'b0), .preset(preset));
  Register #(.width(32), .trigger("rising"), .Select("low")) register_31 (
    .D(Din), .en(demultiplexer_1_out1), .Q(Reg1), .clk(clk), .clr(clear), .cs(1'b0), .preset(preset));
  Register #(.width(32), .trigger("rising"), .Select("low")) register_32 (
    .D(Din), .en(1'b0), .Q(Reg0), .clk(clk), .clr(clear));
  Multiplexer #(.select(5), .width(32), .disabled("Z"), .enable("false")) multiplexer_1 (
    .in0(Reg0), .in1(Reg1), .in2(Reg2), .in3(Reg3), .in4(Reg4), .in5(Reg5), .in6(Reg6), .in7(Reg7),
    .in8(Reg8), .in9(Reg9), .in10(Reg10), .in11(Reg11), .in12(Reg12), .in13(Reg13), .in14(Reg14),
    .in15(Reg15), .in16(register_16_q), .in17(register_15_q), .in18(register_14_q), .in19(register_13_q),
    .in20(register_12_q), .in21(register_11_q), .in22(register_10_q), .in23(register_9_q),
    .in24(register_8_q), .in25(register_7_q), .in26(register_6_q), .in27(register_5_q), .in28(register_4_q),
    .in29(register_3_q), .in30(register_2_q), .in31(register_1_q), .out(RD1), .sel(AddrRead1));
  Multiplexer #(.select(5), .width(32), .disabled("Z"), .enable("false")) multiplexer_2 (
    .in0(Reg0), .in1(Reg1), .in2(Reg2), .in3(Reg3), .in4(Reg4), .in5(Reg5), .in6(Reg6), .in7(Reg7),
    .in8(Reg8), .in9(Reg9), .in10(Reg10), .in11(Reg11), .in12(Reg12), .in13(Reg13), .in14(Reg14),
    .in15(Reg15), .in16(register_16_q), .in17(register_15_q), .in18(register_14_q), .in19(register_13_q),
    .in20(register_12_q), .in21(register_11_q), .in22(register_10_q), .in23(register_9_q),
    .in24(register_8_q), .in25(register_7_q), .in26(register_6_q), .in27(register_5_q), .in28(register_4_q),
    .in29(register_3_q), .in30(register_2_q), .in31(register_1_q), .out(RD2), .sel(AddrRead2));
  // Probe on Reg0
  // Probe on Reg0
  // Probe on Reg1
  // Probe on Reg1
  // Probe on Reg2
  // Probe on Reg2
  // Probe on Reg3
  // Probe on Reg3
  // Probe on Reg0
  // Probe on Reg0
  // Probe on Reg1
  // Probe on Reg1
  // Probe on Reg2
  // Probe on Reg2
  // Probe on Reg3
  // Probe on Reg3
  // Probe on Reg4
  // Probe on Reg4
  // Probe on Reg5
  // Probe on Reg5
  // Probe on Reg6
  // Probe on Reg6
  // Probe on Reg7
  // Probe on Reg7
  // Probe on Reg4
  // Probe on Reg4
  // Probe on Reg5
  // Probe on Reg5
  // Probe on Reg6
  // Probe on Reg6
  // Probe on Reg7
  // Probe on Reg7
  // Probe on Reg8
  // Probe on Reg8
  // Probe on Reg9
  // Probe on Reg9
  // Probe on Reg10
  // Probe on Reg10
  // Probe on Reg11
  // Probe on Reg11
  // Probe on Reg8
  // Probe on Reg8
  // Probe on Reg9
  // Probe on Reg9
  // Probe on Reg10
  // Probe on Reg10
  // Probe on Reg11
  // Probe on Reg11
  // Probe on Reg12
  // Probe on Reg12
  // Probe on Reg13
  // Probe on Reg13
  // Probe on Reg14
  // Probe on Reg14
  // Probe on Reg15
  // Probe on Reg15
  // Probe on Reg12
  // Probe on Reg12
  // Probe on Reg13
  // Probe on Reg13
  // Probe on Reg14
  // Probe on Reg14
  // Probe on Reg15
  // Probe on Reg15

  // Notes on the sheet:
  //   sign
  //   unsign
  //   sign
  //   unsign
  //   sign
  //   unsign
  //   sign
  //   unsign
  //   sign
  //   unsign
  //   sign
  //   unsign
  //   sign
  //   unsign
  //   sign
  //   unsign
  //   sign
  //   unsign
  //   sign
  //   unsign
  //   sign
  //   unsign
  //   sign
  //   unsign
  //   sign
  //   unsign
  //   sign
  //   unsign
  //   sign
  //   unsign
  //   sign
  //   unsign
endmodule

// ALU
module _19071110ALU (
  input  [31:0] A,
  input  [31:0] B,
  input  [1:0] ALUOp,
  output [31:0] out,
  output out_5
);

  wire [31:0] and_1_out, n19071110adder_1_sum, n19071110subtractor_1_difference, or_1_out;

  _19071110Adder u_19071110adder_1 (.B(A), .A(B), .Cin(1'b0), .sum(n19071110adder_1_sum));  // open: Cout
  _19071110Subtractor u_19071110subtractor_1 (
    .X(A), .Y(B), .Bin(1'b0), .difference(n19071110subtractor_1_difference));  // open: Bout
  assign and_1_out = A & B;  // AND_Gate and_1, 32 bits wide
  assign or_1_out = A | B;  // OR_Gate or_1, 32 bits wide
  Multiplexer #(.select(2), .width(32), .disabled("Z"), .enable("false")) multiplexer_1 (
    .in0(n19071110adder_1_sum), .in1(n19071110subtractor_1_difference), .in2(and_1_out), .in3(or_1_out),
    .out(out), .sel(ALUOp));
  _19071110IsZero u_19071110iszero_1 (.x(out), .zero(out_5));
endmodule

// IsZero
module _19071110IsZero (
  input  [31:0] x,
  output zero
);

  wire [1:0] or_4_out;
  wire [3:0] or_2_out;
  wire [7:0] or_3_out;
  wire [15:0] or_1_out;

  assign or_1_out = x[15:0] | x[31:16];  // OR_Gate or_1, 16 bits wide
  assign or_2_out = or_3_out[3:0] | or_3_out[7:4];  // OR_Gate or_2, 4 bits wide
  assign or_3_out = or_1_out[7:0] | or_1_out[15:8];  // OR_Gate or_3, 8 bits wide
  assign or_4_out = or_2_out[1:0] | or_2_out[3:2];  // OR_Gate or_4, 2 bits wide
  nor nor_1 (zero, or_4_out[0], or_4_out[1]);
endmodule

// Sub
module _19071110Subtractor (
  input  [31:0] X,
  input  [31:0] Y,
  input  Bin,
  output [31:0] difference,
  output Bout
);

  wire n19071110adder_1_cout, not_2_out;
  wire [31:0] not_1_out;

  assign not_1_out = ~Y;  // NOT_Gate not_1, 32 bits wide
  _19071110Adder u_19071110adder_1 (
    .B(X), .A(not_1_out), .Cin(not_2_out), .sum(difference), .Cout(n19071110adder_1_cout));
  not not_2 (not_2_out, Bin);
  not not_3 (Bout, n19071110adder_1_cout);
endmodule

// Adder
module _19071110Adder (
  input  [31:0] B,
  input  [31:0] A,
  input  Cin,
  output [31:0] sum,
  output Cout
);

  wire [5:0] bit_extender_1_out, bit_extender_2_out, n19071110abtog_p_6_g_star, n19071110abtog_p_6_p_star,
       n19071110adder6_1_sum, n19071110carrygenerator_1_carry;

  assign bit_extender_1_out = {{4{A[31]}}, A[31:30]};  // Bit_Extender bit_extender_1
  assign bit_extender_2_out = {{4{B[31]}}, B[31:30]};  // Bit_Extender bit_extender_2
  _19071110ABToG_P u_19071110abtog_p_1 (
    .A(bit_extender_1_out), .B(bit_extender_2_out), .P_star(n19071110abtog_p_6_p_star[5]),
    .G_star(n19071110abtog_p_6_g_star[5]));
  _19071110ABToG_P u_19071110abtog_p_2 (
    .A(A[29:24]), .B(B[29:24]), .P_star(n19071110abtog_p_6_p_star[4]), .G_star(n19071110abtog_p_6_g_star[4]));
  _19071110ABToG_P u_19071110abtog_p_3 (
    .A(A[23:18]), .B(B[23:18]), .P_star(n19071110abtog_p_6_p_star[3]), .G_star(n19071110abtog_p_6_g_star[3]));
  _19071110ABToG_P u_19071110abtog_p_4 (
    .A(A[17:12]), .B(B[17:12]), .P_star(n19071110abtog_p_6_p_star[2]), .G_star(n19071110abtog_p_6_g_star[2]));
  _19071110ABToG_P u_19071110abtog_p_5 (
    .A(A[11:6]), .B(B[11:6]), .P_star(n19071110abtog_p_6_p_star[1]), .G_star(n19071110abtog_p_6_g_star[1]));
  _19071110ABToG_P u_19071110abtog_p_6 (
    .A(A[5:0]), .B(B[5:0]), .P_star(n19071110abtog_p_6_p_star[0]), .G_star(n19071110abtog_p_6_g_star[0]));
  Bit_Extender #(.in_width(6), .out_width(2), .\type ("sign")) bit_extender_3 (
    .in(n19071110adder6_1_sum), .out(sum[31:30]));
  _19071110Adder6 u_19071110adder6_1 (
    .Cin(n19071110carrygenerator_1_carry[5]), .A(bit_extender_1_out), .B(bit_extender_2_out),
    .sum(n19071110adder6_1_sum));  // open: Cout
  _19071110Adder6 u_19071110adder6_2 (
    .Cin(n19071110carrygenerator_1_carry[4]), .A(A[29:24]), .B(B[29:24]), .sum(sum[29:24]));  // open: Cout
  _19071110Adder6 u_19071110adder6_3 (
    .Cin(n19071110carrygenerator_1_carry[3]), .A(A[23:18]), .B(B[23:18]), .sum(sum[23:18]));  // open: Cout
  _19071110Adder6 u_19071110adder6_4 (
    .Cin(n19071110carrygenerator_1_carry[2]), .A(A[17:12]), .B(B[17:12]), .sum(sum[17:12]));  // open: Cout
  _19071110Adder6 u_19071110adder6_5 (
    .Cin(n19071110carrygenerator_1_carry[1]), .A(A[11:6]), .B(B[11:6]), .sum(sum[11:6]));  // open: Cout
  _19071110Adder6 u_19071110adder6_6 (
    .Cin(n19071110carrygenerator_1_carry[0]), .A(A[5:0]), .B(B[5:0]), .sum(sum[5:0]));  // open: Cout
  _19071110CarryGenerator u_19071110carrygenerator_1 (
    .G(n19071110abtog_p_6_g_star), .P(n19071110abtog_p_6_p_star), .Cin(Cin),
    .carry(n19071110carrygenerator_1_carry), .Cout(Cout));
endmodule

// Adder6
module _19071110Adder6 (
  input  [5:0] A,
  input  [5:0] B,
  input  Cin,
  output [5:0] sum,
  output Cout
);

  wire [5:0] n19071110abtogp_6_g, n19071110abtogp_6_p, n19071110carrygenerator_1_carry;

  _19071110ABToGP u_19071110abtogp_1 (.A(A[5]), .B(B[5]), .G(n19071110abtogp_6_g[5]), .P(n19071110abtogp_6_p[5]));
  _19071110ABToGP u_19071110abtogp_2 (.A(A[4]), .B(B[4]), .G(n19071110abtogp_6_g[4]), .P(n19071110abtogp_6_p[4]));
  _19071110ABToGP u_19071110abtogp_3 (.A(A[3]), .B(B[3]), .G(n19071110abtogp_6_g[3]), .P(n19071110abtogp_6_p[3]));
  _19071110ABToGP u_19071110abtogp_4 (.A(A[2]), .B(B[2]), .G(n19071110abtogp_6_g[2]), .P(n19071110abtogp_6_p[2]));
  _19071110ABToGP u_19071110abtogp_5 (.A(A[1]), .B(B[1]), .G(n19071110abtogp_6_g[1]), .P(n19071110abtogp_6_p[1]));
  _19071110ABToGP u_19071110abtogp_6 (.A(A[0]), .B(B[0]), .G(n19071110abtogp_6_g[0]), .P(n19071110abtogp_6_p[0]));
  _19071110Adder1 u_19071110adder1_1 (
    .A(A[5]), .B(B[5]), .Cin(n19071110carrygenerator_1_carry[5]), .S(sum[5]));  // open: Cout
  _19071110Adder1 u_19071110adder1_2 (
    .A(A[4]), .B(B[4]), .Cin(n19071110carrygenerator_1_carry[4]), .S(sum[4]));  // open: Cout
  _19071110Adder1 u_19071110adder1_3 (
    .A(A[3]), .B(B[3]), .Cin(n19071110carrygenerator_1_carry[3]), .S(sum[3]));  // open: Cout
  _19071110Adder1 u_19071110adder1_4 (
    .A(A[2]), .B(B[2]), .Cin(n19071110carrygenerator_1_carry[2]), .S(sum[2]));  // open: Cout
  _19071110Adder1 u_19071110adder1_5 (
    .A(A[1]), .B(B[1]), .Cin(n19071110carrygenerator_1_carry[1]), .S(sum[1]));  // open: Cout
  _19071110Adder1 u_19071110adder1_6 (
    .A(A[0]), .B(B[0]), .Cin(n19071110carrygenerator_1_carry[0]), .S(sum[0]));  // open: Cout
  _19071110CarryGenerator u_19071110carrygenerator_1 (
    .G(n19071110abtogp_6_g), .P(n19071110abtogp_6_p), .Cin(Cin), .carry(n19071110carrygenerator_1_carry),
    .Cout(Cout));
endmodule

// Adder1
module _19071110Adder1 (
  input  A,
  input  B,
  input  Cin,
  output S,
  output Cout
);

  wire and_1_out, and_2_out, xor_1_out;

  xor xor_1 (xor_1_out, A, B);
  and and_1 (and_1_out, A, B);
  xor xor_2 (S, xor_1_out, Cin);
  and and_2 (and_2_out, xor_1_out, Cin);
  or or_1 (Cout, and_2_out, and_1_out);
endmodule

// CarryGen
module _19071110CarryGenerator (
  input  [5:0] G,
  input  [5:0] P,
  input  Cin,
  output [5:0] carry,
  output Cout
);

  wire and_1_out, and_2_out, and_3_out, and_4_out, and_5_out, and_6_out, and_7_out, and_8_out, and_9_out,
       and_10_out, and_11_out, and_12_out, and_13_out, and_14_out, and_15_out, and_16_out, and_17_out,
       and_18_out, and_19_out, and_20_out, and_21_out;

  and and_1 (and_1_out, P[5], and_4_out);
  and and_2 (and_2_out, P[5], and_3_out);
  and and_3 (and_3_out, P[4], and_6_out);
  and and_4 (and_4_out, P[4], and_5_out);
  and and_5 (and_5_out, P[3], and_7_out);
  and and_6 (and_6_out, P[3], and_8_out);
  and and_7 (and_7_out, P[2], and_9_out);
  and and_8 (and_8_out, P[2], and_10_out);
  and and_9 (and_9_out, P[1], and_11_out);
  and and_10 (and_10_out, P[1], G[0]);
  and and_11 (and_11_out, Cin, P[0]);
  and and_12 (and_12_out, P[5], and_13_out);
  and and_13 (and_13_out, P[4], and_14_out);
  and and_14 (and_14_out, P[3], and_15_out);
  and and_15 (and_15_out, P[2], G[1]);
  and and_16 (and_16_out, P[5], and_18_out);
  and and_17 (and_17_out, P[5], and_19_out);
  and and_18 (and_18_out, P[4], G[3]);
  and and_19 (and_19_out, P[4], and_20_out);
  and and_20 (and_20_out, P[3], G[2]);
  and and_21 (and_21_out, P[5], G[4]);
  or or_1 (Cout, G[5], and_21_out, and_16_out, and_17_out, and_12_out, and_2_out, and_1_out);
  or or_2 (carry[5], G[4], and_18_out, and_19_out, and_13_out, and_3_out, and_4_out);
  or or_3 (carry[4], G[3], and_20_out, and_14_out, and_6_out, and_5_out);
  or or_4 (carry[3], G[2], and_15_out, and_8_out, and_7_out);
  or or_5 (carry[2], G[1], and_10_out, and_9_out);
  or or_6 (carry[1], G[0], and_11_out);

  assign carry[0] = Cin;
endmodule

// ABG*P*
module _19071110ABToG_P (
  input  [5:0] A,
  input  [5:0] B,
  output P_star,
  output G_star
);

  wire and_1_out, and_2_out, and_3_out, and_4_out, and_5_out, and_6_out, and_7_out, and_8_out, and_9_out,
       n19071110abtogp_1_g, n19071110abtogp_1_p, n19071110abtogp_2_g, n19071110abtogp_2_p,
       n19071110abtogp_3_g, n19071110abtogp_3_p, n19071110abtogp_4_g, n19071110abtogp_4_p,
       n19071110abtogp_5_g, n19071110abtogp_5_p, n19071110abtogp_6_g, n19071110abtogp_6_p;

  _19071110ABToGP u_19071110abtogp_1 (.A(A[5]), .B(B[5]), .G(n19071110abtogp_1_g), .P(n19071110abtogp_1_p));
  _19071110ABToGP u_19071110abtogp_2 (.A(A[4]), .B(B[4]), .G(n19071110abtogp_2_g), .P(n19071110abtogp_2_p));
  _19071110ABToGP u_19071110abtogp_3 (.A(A[3]), .B(B[3]), .G(n19071110abtogp_3_g), .P(n19071110abtogp_3_p));
  _19071110ABToGP u_19071110abtogp_4 (.A(A[2]), .B(B[2]), .G(n19071110abtogp_4_g), .P(n19071110abtogp_4_p));
  _19071110ABToGP u_19071110abtogp_5 (.A(A[1]), .B(B[1]), .G(n19071110abtogp_5_g), .P(n19071110abtogp_5_p));
  _19071110ABToGP u_19071110abtogp_6 (.A(A[0]), .B(B[0]), .G(n19071110abtogp_6_g), .P(n19071110abtogp_6_p));
  and and_1 (and_1_out, n19071110abtogp_5_p, and_4_out);
  and and_2 (and_2_out, and_1_out, n19071110abtogp_6_g);
  and and_3 (and_3_out, n19071110abtogp_3_p, and_7_out);
  and and_4 (and_4_out, n19071110abtogp_4_p, and_3_out);
  and and_5 (and_5_out, and_4_out, n19071110abtogp_5_g);
  and and_6 (and_6_out, and_3_out, n19071110abtogp_4_g);
  and and_7 (and_7_out, n19071110abtogp_2_p, n19071110abtogp_1_p);
  and and_8 (and_8_out, n19071110abtogp_1_p, n19071110abtogp_2_g);
  and and_9 (and_9_out, and_7_out, n19071110abtogp_3_g);
  and and_10 (P_star, n19071110abtogp_6_p, n19071110abtogp_5_p, n19071110abtogp_4_p, n19071110abtogp_3_p, n19071110abtogp_2_p, n19071110abtogp_1_p);
  or or_1 (G_star, n19071110abtogp_1_g, and_8_out, and_9_out, and_6_out, and_5_out, and_2_out);
endmodule

// ABGP
module _19071110ABToGP (
  input  A,
  input  B,
  output G,
  output P
);

  and and_1 (G, A, B);
  xor xor_1 (P, B, A);
endmodule

module _19071110CommandCollector (
  input  RegDst,
  input  ALUSrc,
  input  Mem2Reg,
  input  RegWrite,
  input  MemWrite,
  input  nPCSel,
  input  ExtOp,
  input  [1:0] ALUOp,
  output [8:0] signals
);


  assign signals = {RegDst, ALUSrc, Mem2Reg, RegWrite, MemWrite, nPCSel, ExtOp, ALUOp};
endmodule
