// Logisim project PCOAssignment.circ as structural Verilog: 12 circuits, main circuit 19071110main
module _19071110main (
);

  _19071110ALU u_19071110alu_1 ();  // open: A, B, sel, out, out_5
endmodule

module _19071110RegFile (
  input  enable,
  input  clear,
  input  preset,
  input  [31:0] Din,
  input  [4:0] AddrWrite,
  input  selectAll,
  output [31:0] Dout
);

  wire clk_out, decoder_1_out0, decoder_1_out1, decoder_1_out2, decoder_1_out3, decoder_1_out4,
       decoder_1_out5, decoder_1_out6, decoder_1_out7, decoder_1_out8, decoder_1_out9, decoder_1_out10,
       decoder_1_out11, decoder_1_out12, decoder_1_out13, decoder_1_out14, decoder_1_out15, decoder_1_out16,
       decoder_1_out17, decoder_1_out18, decoder_1_out19, decoder_1_out20, decoder_1_out21, decoder_1_out22,
       decoder_1_out23, decoder_1_out24, decoder_1_out25, decoder_1_out26, decoder_1_out27, decoder_1_out28,
       decoder_1_out29, decoder_1_out30, decoder_1_out31, nor_1_out, nor_2_out, nor_3_out, nor_4_out,
       nor_5_out, nor_6_out, nor_7_out, nor_8_out, nor_9_out, nor_10_out, nor_11_out, nor_12_out, nor_13_out,
       nor_14_out, nor_15_out, nor_16_out, nor_17_out, nor_18_out, nor_19_out, nor_20_out, nor_21_out,
       nor_22_out, nor_23_out, nor_24_out, nor_25_out, nor_26_out, nor_27_out, nor_28_out, nor_29_out,
       nor_30_out, nor_31_out, nor_32_out;
  wire [31:0] register_3_q, register_4_q, register_5_q, register_6_q, register_7_q, register_8_q,
       register_9_q, register_10_q, register_11_q, register_12_q, register_13_q, register_14_q,
       register_15_q, register_16_q, register_17_q, register_18_q, register_19_q, register_20_q,
       register_21_q, register_22_q, register_23_q, register_24_q, register_25_q, register_26_q,
       register_27_q, register_28_q, register_29_q, register_30_q, register_31_q, register_32_q;

  Decoder #(.select(5), .tristate("false"), .disabled("Z"), .enable("false")) decoder_1 (
    .out0(decoder_1_out0), .out1(decoder_1_out1), .out2(decoder_1_out2), .out3(decoder_1_out3),
    .out4(decoder_1_out4), .out5(decoder_1_out5), .out6(decoder_1_out6), .out7(decoder_1_out7),
    .out8(decoder_1_out8), .out9(decoder_1_out9), .out10(decoder_1_out10), .out11(decoder_1_out11),
    .out12(decoder_1_out12), .out13(decoder_1_out13), .out14(decoder_1_out14), .out15(decoder_1_out15),
    .out16(decoder_1_out16), .out17(decoder_1_out17), .out18(decoder_1_out18), .out19(decoder_1_out19),
    .out20(decoder_1_out20), .out21(decoder_1_out21), .out22(decoder_1_out22), .out23(decoder_1_out23),
    .out24(decoder_1_out24), .out25(decoder_1_out25), .out26(decoder_1_out26), .out27(decoder_1_out27),
    .out28(decoder_1_out28), .out29(decoder_1_out29), .out30(decoder_1_out30), .out31(decoder_1_out31),
    .sel(AddrWrite));
  Clock #(.highDuration(1), .lowDuration(1)) clk (.out(clk_out));
  nor nor_1 (nor_1_out, decoder_1_out31, selectAll);
  nor nor_2 (nor_2_out, decoder_1_out30, selectAll);
  nor nor_3 (nor_3_out, decoder_1_out29, selectAll);
  nor nor_4 (nor_4_out, decoder_1_out28, selectAll);
  nor nor_5 (nor_5_out, decoder_1_out27, selectAll);
  nor nor_6 (nor_6_out, decoder_1_out26, selectAll);
  nor nor_7 (nor_7_out, decoder_1_out25, selectAll);
  nor nor_8 (nor_8_out, decoder_1_out24, selectAll);
  nor nor_9 (nor_9_out, decoder_1_out23, selectAll);
  nor nor_10 (nor_10_out, decoder_1_out22, selectAll);
  nor nor_11 (nor_11_out, decoder_1_out21, selectAll);
  nor nor_12 (nor_12_out, decoder_1_out20, selectAll);
  nor nor_13 (nor_13_out, decoder_1_out19, selectAll);
  nor nor_14 (nor_14_out, decoder_1_out18, selectAll);
  nor nor_15 (nor_15_out, decoder_1_out17, selectAll);
  nor nor_16 (nor_16_out, decoder_1_out16, selectAll);
  nor nor_17 (nor_17_out, decoder_1_out15, selectAll);
  nor nor_18 (nor_18_out, decoder_1_out14, selectAll);
  nor nor_19 (nor_19_out, decoder_1_out13, selectAll);
  nor nor_20 (nor_20_out, decoder_1_out12, selectAll);
  nor nor_21 (nor_21_out, decoder_1_out11, selectAll);
  nor nor_22 (nor_22_out, decoder_1_out10, selectAll);
  nor nor_23 (nor_23_out, decoder_1_out9, selectAll);
  nor nor_24 (nor_24_out, decoder_1_out8, selectAll);
  nor nor_25 (nor_25_out, decoder_1_out7, selectAll);
  nor nor_26 (nor_26_out, decoder_1_out6, selectAll);
  nor nor_27 (nor_27_out, decoder_1_out5, selectAll);
  nor nor_28 (nor_28_out, decoder_1_out4, selectAll);
  nor nor_29 (nor_29_out, decoder_1_out3, selectAll);
  nor nor_30 (nor_30_out, decoder_1_out2, selectAll);
  nor nor_31 (nor_31_out, decoder_1_out1, selectAll);
  nor nor_32 (nor_32_out, decoder_1_out0, selectAll);
  Register #(.width(32), .trigger("rising"), .Select("low")) register_1 (
    .D(Din), .en(enable), .Q(Dout), .clk(clk_out), .clr(clear), .cs(nor_1_out), .preset(preset));
  Register #(.width(32), .trigger("rising"), .Select("low")) register_2 (
    .D(Din), .en(enable), .Q(Dout), .clk(clk_out), .clr(clear), .cs(nor_2_out), .preset(preset));
  Register #(.width(32), .trigger("rising"), .Select("low")) register_3 (
    .D(Din), .en(enable), .Q(register_3_q), .clk(clk_out), .clr(clear), .cs(nor_3_out), .preset(preset));
  Register #(.width(32), .trigger("rising"), .Select("low")) register_4 (
    .D(Din), .en(enable), .Q(register_4_q), .clk(clk_out), .clr(clear), .cs(nor_4_out), .preset(preset));
  Register #(.width(32), .trigger("rising"), .Select("low")) register_5 (
    .D(Din), .en(enable), .Q(register_5_q), .clk(clk_out), .clr(clear), .cs(nor_5_out), .preset(preset));
  Register #(.width(32), .trigger("rising"), .Select("low")) register_6 (
    .D(Din), .en(enable), .Q(register_6_q), .clk(clk_out), .clr(clear), .cs(nor_6_out), .preset(preset));
  Register #(.width(32), .trigger("rising"), .Select("low")) register_7 (
    .D(Din), .en(enable), .Q(register_7_q), .clk(clk_out), .clr(clear), .cs(nor_7_out), .preset(preset));
  Register #(.width(32), .trigger("rising"), .Select("low")) register_8 (
    .D(Din), .en(enable), .Q(register_8_q), .clk(clk_out), .clr(clear), .cs(nor_8_out), .preset(preset));
  Register #(.width(32), .trigger("rising"), .Select("low")) register_9 (
    .D(Din), .en(enable), .Q(register_9_q), .clk(clk_out), .clr(clear), .cs(nor_9_out), .preset(preset));
  Register #(.width(32), .trigger("rising"), .Select("low")) register_10 (
    .D(Din), .en(enable), .Q(register_10_q), .clk(clk_out), .clr(clear), .cs(nor_10_out), .preset(preset));
  Register #(.width(32), .trigger("rising"), .Select("low")) register_11 (
    .D(Din), .en(enable), .Q(register_11_q), .clk(clk_out), .clr(clear), .cs(nor_11_out), .preset(preset));
  Register #(.width(32), .trigger("rising"), .Select("low")) register_12 (
    .D(Din), .en(enable), .Q(register_12_q), .clk(clk_out), .clr(clear), .cs(nor_12_out), .preset(preset));
  Register #(.width(32), .trigger("rising"), .Select("low")) register_13 (
    .D(Din), .en(enable), .Q(register_13_q), .clk(clk_out), .clr(clear), .cs(nor_13_out), .preset(preset));
  Register #(.width(32), .trigger("rising"), .Select("low")) register_14 (
    .D(Din), .en(enable), .Q(register_14_q), .clk(clk_out), .clr(clear), .cs(nor_14_out), .preset(preset));
  Register #(.width(32), .trigger("rising"), .Select("low")) register_15 (
    .D(Din), .en(enable), .Q(register_15_q), .clk(clk_out), .clr(clear), .cs(nor_15_out), .preset(preset));
  Register #(.width(32), .trigger("rising"), .Select("low")) register_16 (
    .D(Din), .en(enable), .Q(register_16_q), .clk(clk_out), .clr(clear), .cs(nor_16_out), .preset(preset));
  Register #(.width(32), .trigger("rising"), .Select("low")) register_17 (
    .D(Din), .en(enable), .Q(register_17_q), .clk(clk_out), .clr(clear), .cs(nor_17_out), .preset(preset));
  Register #(.width(32), .trigger("rising"), .Select("low")) register_18 (
    .D(Din), .en(enable), .Q(register_18_q), .clk(clk_out), .clr(clear), .cs(nor_18_out), .preset(preset));
  Register #(.width(32), .trigger("rising"), .Select("low")) register_19 (
    .D(Din), .en(enable), .Q(register_19_q), .clk(clk_out), .clr(clear), .cs(nor_19_out), .preset(preset));
  Register #(.width(32), .trigger("rising"), .Select("low")) register_20 (
    .D(Din), .en(enable), .Q(register_20_q), .clk(clk_out), .clr(clear), .cs(nor_20_out), .preset(preset));
  Register #(.width(32), .trigger("rising"), .Select("low")) register_21 (
    .D(Din), .en(enable), .Q(register_21_q), .clk(clk_out), .clr(clear), .cs(nor_21_out), .preset(preset));
  Register #(.width(32), .trigger("rising"), .Select("low")) register_22 (
    .D(Din), .en(enable), .Q(register_22_q), .clk(clk_out), .clr(clear), .cs(nor_22_out), .preset(preset));
  Register #(.width(32), .trigger("rising"), .Select("low")) register_23 (
    .D(Din), .en(enable), .Q(register_23_q), .clk(clk_out), .clr(clear), .cs(nor_23_out), .preset(preset));
  Register #(.width(32), .trigger("rising"), .Select("low")) register_24 (
    .D(Din), .en(enable), .Q(register_24_q), .clk(clk_out), .clr(clear), .cs(nor_24_out), .preset(preset));
  Register #(.width(32), .trigger("rising"), .Select("low")) register_25 (
    .D(Din), .en(enable), .Q(register_25_q), .clk(clk_out), .clr(clear), .cs(nor_25_out), .preset(preset));
  Register #(.width(32), .trigger("rising"), .Select("low")) register_26 (
    .D(Din), .en(enable), .Q(register_26_q), .clk(clk_out), .clr(clear), .cs(nor_26_out), .preset(preset));
  Register #(.width(32), .trigger("rising"), .Select("low")) register_27 (
    .D(Din), .en(enable), .Q(register_27_q), .clk(clk_out), .clr(clear), .cs(nor_27_out), .preset(preset));
  Register #(.width(32), .trigger("rising"), .Select("low")) register_28 (
    .D(Din), .en(enable), .Q(register_28_q), .clk(clk_out), .clr(clear), .cs(nor_28_out), .preset(preset));
  Register #(.width(32), .trigger("rising"), .Select("low")) register_29 (
    .D(Din), .en(enable), .Q(register_29_q), .clk(clk_out), .clr(clear), .cs(nor_29_out), .preset(preset));
  Register #(.width(32), .trigger("rising"), .Select("low")) register_30 (
    .D(Din), .en(enable), .Q(register_30_q), .clk(clk_out), .clr(clear), .cs(nor_30_out), .preset(preset));
  Register #(.width(32), .trigger("rising"), .Select("low")) register_31 (
    .D(Din), .en(enable), .Q(register_31_q), .clk(clk_out), .clr(clear), .cs(nor_31_out), .preset(preset));
  Register #(.width(32), .trigger("rising"), .Select("low")) register_32 (
    .D(Din), .en(enable), .Q(register_32_q), .clk(clk_out), .clr(clear), .cs(nor_32_out), .preset(preset));
endmodule

// ALU
module _19071110ALU (
  input  [31:0] A,
  input  [31:0] B,
  input  [1:0] sel,
  output [31:0] out,
  output out_5
);

  wire [31:0] and_1_out, n19071110adder_1_sum, n19071110subtractor_1_difference, or_1_out;

  _19071110Adder u_19071110adder_1 (.B(A), .A(B), .Cin(1'b0), .sum(n19071110adder_1_sum));  // open: Cout
  _19071110Subtractor u_19071110subtractor_1 (
    .X(A), .Y(B), .Bin(1'b0), .difference(n19071110subtractor_1_difference));  // open: Bout
  assign and_1_out = A & B;  // AND_Gate and_1, 32 bits wide
  assign or_1_out = A | B;  // OR_Gate or_1, 32 bits wide
  Multiplexer #(.select(2), .width(32), .disabled("Z"), .enable("false")) multiplexer_1 (
    .in0(n19071110adder_1_sum), .in1(n19071110subtractor_1_difference), .in2(and_1_out), .in3(or_1_out),
    .out(out), .sel(sel));
  _19071110IsZero u_19071110iszero_1 (.x(out), .zero(out_5));
endmodule

// IsZero
module _19071110IsZero (
  input  [31:0] x,
  output zero
);

  wire [1:0] or_4_out;
  wire [3:0] or_2_out;
  wire [7:0] or_3_out;
  wire [15:0] or_1_out;

  assign or_1_out = x[15:0] | x[31:16];  // OR_Gate or_1, 16 bits wide
  assign or_2_out = or_3_out[3:0] | or_3_out[7:4];  // OR_Gate or_2, 4 bits wide
  assign or_3_out = or_1_out[7:0] | or_1_out[15:8];  // OR_Gate or_3, 8 bits wide
  assign or_4_out = or_2_out[1:0] | or_2_out[3:2];  // OR_Gate or_4, 2 bits wide
  nor nor_1 (zero, or_4_out[0], or_4_out[1]);
endmodule

// Sub
module _19071110Subtractor (
  input  [31:0] X,
  input  [31:0] Y,
  input  Bin,
  output [31:0] difference,
  output Bout
);

  wire n19071110adder_1_cout, not_2_out;
  wire [31:0] not_1_out;

  assign not_1_out = ~Y;  // NOT_Gate not_1, 32 bits wide
  _19071110Adder u_19071110adder_1 (
    .B(X), .A(not_1_out), .Cin(not_2_out), .sum(difference), .Cout(n19071110adder_1_cout));
  not not_2 (not_2_out, Bin);
  not not_3 (Bout, n19071110adder_1_cout);
endmodule

// Adder
module _19071110Adder (
  input  [31:0] B,
  input  [31:0] A,
  input  Cin,
  output [31:0] sum,
  output Cout
);

  wire [5:0] bit_extender_1_out, bit_extender_2_out, n19071110abtog_p_6_g_star, n19071110abtog_p_6_p_star,
       n19071110adder6_1_sum, n19071110carrygenerator_1_carry;

  assign bit_extender_1_out = {{4{A[31]}}, A[31:30]};  // Bit_Extender bit_extender_1
  assign bit_extender_2_out = {{4{B[31]}}, B[31:30]};  // Bit_Extender bit_extender_2
  _19071110ABToG_P u_19071110abtog_p_1 (
    .A(bit_extender_1_out), .B(bit_extender_2_out), .P_star(n19071110abtog_p_6_p_star[5]),
    .G_star(n19071110abtog_p_6_g_star[5]));
  _19071110ABToG_P u_19071110abtog_p_2 (
    .A(A[29:24]), .B(B[29:24]), .P_star(n19071110abtog_p_6_p_star[4]), .G_star(n19071110abtog_p_6_g_star[4]));
  _19071110ABToG_P u_19071110abtog_p_3 (
    .A(A[23:18]), .B(B[23:18]), .P_star(n19071110abtog_p_6_p_star[3]), .G_star(n19071110abtog_p_6_g_star[3]));
  _19071110ABToG_P u_19071110abtog_p_4 (
    .A(A[17:12]), .B(B[17:12]), .P_star(n19071110abtog_p_6_p_star[2]), .G_star(n19071110abtog_p_6_g_star[2]));
  _19071110ABToG_P u_19071110abtog_p_5 (
    .A(A[11:6]), .B(B[11:6]), .P_star(n19071110abtog_p_6_p_star[1]), .G_star(n19071110abtog_p_6_g_star[1]));
  _19071110ABToG_P u_19071110abtog_p_6 (
    .A(A[5:0]), .B(B[5:0]), .P_star(n19071110abtog_p_6_p_star[0]), .G_star(n19071110abtog_p_6_g_star[0]));
  Bit_Extender #(.in_width(6), .out_width(2), .\type ("sign")) bit_extender_3 (
    .in(n19071110adder6_1_sum), .out(sum[31:30]));
  _19071110Adder6 u_19071110adder6_1 (
    .Cin(n19071110carrygenerator_1_carry[5]), .A(bit_extender_1_out), .B(bit_extender_2_out),
    .sum(n19071110adder6_1_sum));  // open: Cout
  _19071110Adder6 u_19071110adder6_2 (
    .Cin(n19071110carrygenerator_1_carry[4]), .A(A[29:24]), .B(B[29:24]), .sum(sum[29:24]));  // open: Cout
  _19071110Adder6 u_19071110adder6_3 (
    .Cin(n19071110carrygenerator_1_carry[3]), .A(A[23:18]), .B(B[23:18]), .sum(sum[23:18]));  // open: Cout
  _19071110Adder6 u_19071110adder6_4 (
    .Cin(n19071110carrygenerator_1_carry[2]), .A(A[17:12]), .B(B[17:12]), .sum(sum[17:12]));  // open: Cout
  _19071110Adder6 u_19071110adder6_5 (
    .Cin(n19071110carrygenerator_1_carry[1]), .A(A[11:6]), .B(B[11:6]), .sum(sum[11:6]));  // open: Cout
  _19071110Adder6 u_19071110adder6_6 (
    .Cin(n19071110carrygenerator_1_carry[0]), .A(A[5:0]), .B(B[5:0]), .sum(sum[5:0]));  // open: Cout
  _19071110CarryGenerator u_19071110carrygenerator_1 (
    .G(n19071110abtog_p_6_g_star), .P(n19071110abtog_p_6_p_star), .Cin(Cin),
    .carry(n19071110carrygenerator_1_carry), .Cout(Cout));
endmodule

// Adder6
module _19071110Adder6 (
  input  [5:0] A,
  input  [5:0] B,
  input  Cin,
  output [5:0] sum,
  output Cout
);

  wire [5:0] n19071110abtogp_6_g, n19071110abtogp_6_p, n19071110carrygenerator_1_carry;

  _19071110ABToGP u_19071110abtogp_1 (.A(A[5]), .B(B[5]), .G(n19071110abtogp_6_g[5]), .P(n19071110abtogp_6_p[5]));
  _19071110ABToGP u_19071110abtogp_2 (.A(A[4]), .B(B[4]), .G(n19071110abtogp_6_g[4]), .P(n19071110abtogp_6_p[4]));
  _19071110ABToGP u_19071110abtogp_3 (.A(A[3]), .B(B[3]), .G(n19071110abtogp_6_g[3]), .P(n19071110abtogp_6_p[3]));
  _19071110ABToGP u_19071110abtogp_4 (.A(A[2]), .B(B[2]), .G(n19071110abtogp_6_g[2]), .P(n19071110abtogp_6_p[2]));
  _19071110ABToGP u_19071110abtogp_5 (.A(A[1]), .B(B[1]), .G(n19071110abtogp_6_g[1]), .P(n19071110abtogp_6_p[1]));
  _19071110ABToGP u_19071110abtogp_6 (.A(A[0]), .B(B[0]), .G(n19071110abtogp_6_g[0]), .P(n19071110abtogp_6_p[0]));
  _19071110Adder1 u_19071110adder1_1 (
    .A(A[5]), .B(B[5]), .Cin(n19071110carrygenerator_1_carry[5]), .S(sum[5]));  // open: Cout
  _19071110Adder1 u_19071110adder1_2 (
    .A(A[4]), .B(B[4]), .Cin(n19071110carrygenerator_1_carry[4]), .S(sum[4]));  // open: Cout
  _19071110Adder1 u_19071110adder1_3 (
    .A(A[3]), .B(B[3]), .Cin(n19071110carrygenerator_1_carry[3]), .S(sum[3]));  // open: Cout
  _19071110Adder1 u_19071110adder1_4 (
    .A(A[2]), .B(B[2]), .Cin(n19071110carrygenerator_1_carry[2]), .S(sum[2]));  // open: Cout
  _19071110Adder1 u_19071110adder1_5 (
    .A(A[1]), .B(B[1]), .Cin(n19071110carrygenerator_1_carry[1]), .S(sum[1]));  // open: Cout
  _19071110Adder1 u_19071110adder1_6 (
    .A(A[0]), .B(B[0]), .Cin(n19071110carrygenerator_1_carry[0]), .S(sum[0]));  // open: Cout
  _19071110CarryGenerator u_19071110carrygenerator_1 (
    .G(n19071110abtogp_6_g), .P(n19071110abtogp_6_p), .Cin(Cin), .carry(n19071110carrygenerator_1_carry),
    .Cout(Cout));
endmodule

// Adder1
module _19071110Adder1 (
  input  A,
  input  B,
  input  Cin,
  output S,
  output Cout
);

  wire and_1_out, and_2_out, xor_1_out;

  xor xor_1 (xor_1_out, A, B);
  and and_1 (and_1_out, A, B);
  xor xor_2 (S, xor_1_out, Cin);
  and and_2 (and_2_out, xor_1_out, Cin);
  or or_1 (Cout, and_2_out, and_1_out);
endmodule

// CarryGen
module _19071110CarryGenerator (
  input  [5:0] G,
  input  [5:0] P,
  input  Cin,
  output [5:0] carry,
  output Cout
);

  wire and_1_out, and_2_out, and_3_out, and_4_out, and_5_out, and_6_out, and_7_out, and_8_out, and_9_out,
       and_10_out, and_11_out, and_12_out, and_13_out, and_14_out, and_15_out, and_16_out, and_17_out,
       and_18_out, and_19_out, and_20_out, and_21_out;

  and and_1 (and_1_out, P[5], and_3_out);
  and and_2 (and_2_out, P[5], and_4_out);
  and and_3 (and_3_out, P[4], and_5_out);
  and and_4 (and_4_out, P[4], and_6_out);
  and and_5 (and_5_out, P[3], and_7_out);
  and and_6 (and_6_out, P[3], and_8_out);
  and and_7 (and_7_out, P[2], and_10_out);
  and and_8 (and_8_out, P[2], and_9_out);
  and and_9 (and_9_out, P[1], G[0]);
  and and_10 (and_10_out, P[1], and_11_out);
  and and_11 (and_11_out, Cin, P[0]);
  and and_12 (and_12_out, P[5], and_13_out);
  and and_13 (and_13_out, P[4], and_14_out);
  and and_14 (and_14_out, P[3], and_15_out);
  and and_15 (and_15_out, P[2], G[1]);
  and and_16 (and_16_out, P[5], and_18_out);
  and and_17 (and_17_out, P[5], and_19_out);
  and and_18 (and_18_out, P[4], and_20_out);
  and and_19 (and_19_out, P[4], G[3]);
  and and_20 (and_20_out, P[3], G[2]);
  and and_21 (and_21_out, P[5], G[4]);
  or or_1 (Cout, G[5], and_21_out, and_17_out, and_16_out, and_12_out, and_2_out, and_1_out);
  or or_2 (carry[5], G[4], and_19_out, and_18_out, and_13_out, and_4_out, and_3_out);
  or or_3 (carry[4], G[3], and_20_out, and_14_out, and_6_out, and_5_out);
  or or_4 (carry[3], G[2], and_15_out, and_8_out, and_7_out);
  or or_5 (carry[2], G[1], and_9_out, and_10_out);
  or or_6 (carry[1], G[0], and_11_out);

  assign carry[0] = Cin;
endmodule

// ABG*P*
module _19071110ABToG_P (
  input  [5:0] A,
  input  [5:0] B,
  output P_star,
  output G_star
);

  wire and_1_out, and_2_out, and_3_out, and_4_out, and_5_out, and_6_out, and_7_out, and_8_out, and_9_out,
       n19071110abtogp_1_g, n19071110abtogp_1_p, n19071110abtogp_2_g, n19071110abtogp_2_p,
       n19071110abtogp_3_g, n19071110abtogp_3_p, n19071110abtogp_4_g, n19071110abtogp_4_p,
       n19071110abtogp_5_g, n19071110abtogp_5_p, n19071110abtogp_6_g, n19071110abtogp_6_p;

  _19071110ABToGP u_19071110abtogp_1 (.A(A[5]), .B(B[5]), .G(n19071110abtogp_1_g), .P(n19071110abtogp_1_p));
  _19071110ABToGP u_19071110abtogp_2 (.A(A[4]), .B(B[4]), .G(n19071110abtogp_2_g), .P(n19071110abtogp_2_p));
  _19071110ABToGP u_19071110abtogp_3 (.A(A[3]), .B(B[3]), .G(n19071110abtogp_3_g), .P(n19071110abtogp_3_p));
  _19071110ABToGP u_19071110abtogp_4 (.A(A[2]), .B(B[2]), .G(n19071110abtogp_4_g), .P(n19071110abtogp_4_p));
  _19071110ABToGP u_19071110abtogp_5 (.A(A[1]), .B(B[1]), .G(n19071110abtogp_5_g), .P(n19071110abtogp_5_p));
  _19071110ABToGP u_19071110abtogp_6 (.A(A[0]), .B(B[0]), .G(n19071110abtogp_6_g), .P(n19071110abtogp_6_p));
  and and_1 (and_1_out, n19071110abtogp_5_p, and_4_out);
  and and_2 (and_2_out, and_1_out, n19071110abtogp_6_g);
  and and_3 (and_3_out, n19071110abtogp_3_p, and_7_out);
  and and_4 (and_4_out, n19071110abtogp_4_p, and_3_out);
  and and_5 (and_5_out, and_3_out, n19071110abtogp_4_g);
  and and_6 (and_6_out, and_4_out, n19071110abtogp_5_g);
  and and_7 (and_7_out, n19071110abtogp_2_p, n19071110abtogp_1_p);
  and and_8 (and_8_out, n19071110abtogp_1_p, n19071110abtogp_2_g);
  and and_9 (and_9_out, and_7_out, n19071110abtogp_3_g);
  and and_10 (P_star, n19071110abtogp_6_p, n19071110abtogp_5_p, n19071110abtogp_4_p, n19071110abtogp_3_p, n19071110abtogp_2_p, n19071110abtogp_1_p);
  or or_1 (G_star, n19071110abtogp_1_g, and_8_out, and_9_out, and_5_out, and_6_out, and_2_out);
endmodule

// ABGP
module _19071110ABToGP (
  input  A,
  input  B,
  output G,
  output P
);

  and and_1 (G, A, B);
  xor xor_1 (P, B, A);
endmodule

module _19071110GPR (
  input  enable,
  input  clear,
  input  preset,
  input  [4:0] AddrWrite,
  input  [31:0] Din,
  input  [4:0] AddrRead1,
  input  [4:0] AddrRead2,
  output [31:0] RD1,
  output [31:0] RD2
);

  wire clk_out, decoder_1_out0, decoder_1_out1, decoder_1_out2, decoder_1_out3, decoder_1_out4,
       decoder_1_out5, decoder_1_out6, decoder_1_out7, decoder_1_out8, decoder_1_out9, decoder_1_out10,
       decoder_1_out11, decoder_1_out12, decoder_1_out13, decoder_1_out14, decoder_1_out15, decoder_1_out16,
       decoder_1_out17, decoder_1_out18, decoder_1_out19, decoder_1_out20, decoder_1_out21, decoder_1_out22,
       decoder_1_out23, decoder_1_out24, decoder_1_out25, decoder_1_out26, decoder_1_out27, decoder_1_out28,
       decoder_1_out29, decoder_1_out30, decoder_1_out31;
  wire [31:0] register_1_q, register_2_q, register_3_q, register_4_q, register_5_q, register_6_q,
       register_7_q, register_8_q, register_9_q, register_10_q, register_11_q, register_12_q, register_13_q,
       register_14_q, register_15_q, register_16_q, register_17_q, register_18_q, register_19_q,
       register_20_q, register_21_q, register_22_q, register_23_q, register_24_q, register_25_q,
       register_26_q, register_27_q, register_28_q, register_29_q, register_30_q, register_31_q,
       register_32_q;

  Decoder #(.select(5), .tristate("false"), .disabled("Z"), .enable("false")) decoder_1 (
    .out0(decoder_1_out0), .out1(decoder_1_out1), .out2(decoder_1_out2), .out3(decoder_1_out3),
    .out4(decoder_1_out4), .out5(decoder_1_out5), .out6(decoder_1_out6), .out7(decoder_1_out7),
    .out8(decoder_1_out8), .out9(decoder_1_out9), .out10(decoder_1_out10), .out11(decoder_1_out11),
    .out12(decoder_1_out12), .out13(decoder_1_out13), .out14(decoder_1_out14), .out15(decoder_1_out15),
    .out16(decoder_1_out16), .out17(decoder_1_out17), .out18(decoder_1_out18), .out19(decoder_1_out19),
    .out20(decoder_1_out20), .out21(decoder_1_out21), .out22(decoder_1_out22), .out23(decoder_1_out23),
    .out24(decoder_1_out24), .out25(decoder_1_out25), .out26(decoder_1_out26), .out27(decoder_1_out27),
    .out28(decoder_1_out28), .out29(decoder_1_out29), .out30(decoder_1_out30), .out31(decoder_1_out31),
    .sel(AddrWrite));
  Clock #(.highDuration(1), .lowDuration(1)) clk (.out(clk_out));
  Register #(.width(32), .trigger("rising"), .Select("low")) register_1 (
    .D(Din), .en(decoder_1_out31), .Q(register_1_q), .clk(clk_out), .clr(clear), .cs(enable), .preset(preset));
  Register #(.width(32), .trigger("rising"), .Select("low")) register_2 (
    .D(Din), .en(decoder_1_out30), .Q(register_2_q), .clk(clk_out), .clr(clear), .cs(enable), .preset(preset));
  Register #(.width(32), .trigger("rising"), .Select("low")) register_3 (
    .D(Din), .en(decoder_1_out29), .Q(register_3_q), .clk(clk_out), .clr(clear), .cs(enable), .preset(preset));
  Register #(.width(32), .trigger("rising"), .Select("low")) register_4 (
    .D(Din), .en(decoder_1_out28), .Q(register_4_q), .clk(clk_out), .clr(clear), .cs(enable), .preset(preset));
  Register #(.width(32), .trigger("rising"), .Select("low")) register_5 (
    .D(Din), .en(decoder_1_out27), .Q(register_5_q), .clk(clk_out), .clr(clear), .cs(enable), .preset(preset));
  Register #(.width(32), .trigger("rising"), .Select("low")) register_6 (
    .D(Din), .en(decoder_1_out26), .Q(register_6_q), .clk(clk_out), .clr(clear), .cs(enable), .preset(preset));
  Register #(.width(32), .trigger("rising"), .Select("low")) register_7 (
    .D(Din), .en(decoder_1_out25), .Q(register_7_q), .clk(clk_out), .clr(clear), .cs(enable), .preset(preset));
  Register #(.width(32), .trigger("rising"), .Select("low")) register_8 (
    .D(Din), .en(decoder_1_out24), .Q(register_8_q), .clk(clk_out), .clr(clear), .cs(enable), .preset(preset));
  Register #(.width(32), .trigger("rising"), .Select("low")) register_9 (
    .D(Din), .en(decoder_1_out23), .Q(register_9_q), .clk(clk_out), .clr(clear), .cs(enable), .preset(preset));
  Register #(.width(32), .trigger("rising"), .Select("low")) register_10 (
    .D(Din), .en(decoder_1_out22), .Q(register_10_q), .clk(clk_out), .clr(clear), .cs(enable), .preset(preset));
  Register #(.width(32), .trigger("rising"), .Select("low")) register_11 (
    .D(Din), .en(decoder_1_out21), .Q(register_11_q), .clk(clk_out), .clr(clear), .cs(enable), .preset(preset));
  Register #(.width(32), .trigger("rising"), .Select("low")) register_12 (
    .D(Din), .en(decoder_1_out20), .Q(register_12_q), .clk(clk_out), .clr(clear), .cs(enable), .preset(preset));
  Register #(.width(32), .trigger("rising"), .Select("low")) register_13 (
    .D(Din), .en(decoder_1_out19), .Q(register_13_q), .clk(clk_out), .clr(clear), .cs(enable), .preset(preset));
  Register #(.width(32), .trigger("rising"), .Select("low")) register_14 (
    .D(Din), .en(decoder_1_out18), .Q(register_14_q), .clk(clk_out), .clr(clear), .cs(enable), .preset(preset));
  Register #(.width(32), .trigger("rising"), .Select("low")) register_15 (
    .D(Din), .en(decoder_1_out17), .Q(register_15_q), .clk(clk_out), .clr(clear), .cs(enable), .preset(preset));
  Register #(.width(32), .trigger("rising"), .Select("low")) register_16 (
    .D(Din), .en(decoder_1_out16), .Q(register_16_q), .clk(clk_out), .clr(clear), .cs(enable), .preset(preset));
  Register #(.width(32), .trigger("rising"), .Select("low")) register_17 (
    .D(Din), .en(decoder_1_out15), .Q(register_17_q), .clk(clk_out), .clr(clear), .cs(enable), .preset(preset));
  Register #(.width(32), .trigger("rising"), .Select("low")) register_18 (
    .D(Din), .en(decoder_1_out14), .Q(register_18_q), .clk(clk_out), .clr(clear), .cs(enable), .preset(preset));
  Register #(.width(32), .trigger("rising"), .Select("low")) register_19 (
    .D(Din), .en(decoder_1_out13), .Q(register_19_q), .clk(clk_out), .clr(clear), .cs(enable), .preset(preset));
  Register #(.width(32), .trigger("rising"), .Select("low")) register_20 (
    .D(Din), .en(decoder_1_out12), .Q(register_20_q), .clk(clk_out), .clr(clear), .cs(enable), .preset(preset));
  Register #(.width(32), .trigger("rising"), .Select("low")) register_21 (
    .D(Din), .en(decoder_1_out11), .Q(register_21_q), .clk(clk_out), .clr(clear), .cs(enable), .preset(preset));
  Register #(.width(32), .trigger("rising"), .Select("low")) register_22 (
    .D(Din), .en(decoder_1_out10), .Q(register_22_q), .clk(clk_out), .clr(clear), .cs(enable), .preset(preset));
  Register #(.width(32), .trigger("rising"), .Select("low")) register_23 (
    .D(Din), .en(decoder_1_out9), .Q(register_23_q), .clk(clk_out), .clr(clear), .cs(enable), .preset(preset));
  Register #(.width(32), .trigger("rising"), .Select("low")) register_24 (
    .D(Din), .en(decoder_1_out8), .Q(register_24_q), .clk(clk_out), .clr(clear), .cs(enable), .preset(preset));
  Register #(.width(32), .trigger("rising"), .Select("low")) register_25 (
    .D(Din), .en(decoder_1_out7), .Q(register_25_q), .clk(clk_out), .clr(clear), .cs(enable), .preset(preset));
  Register #(.width(32), .trigger("rising"), .Select("low")) register_26 (
    .D(Din), .en(decoder_1_out6), .Q(register_26_q), .clk(clk_out), .clr(clear), .cs(enable), .preset(preset));
  Register #(.width(32), .trigger("rising"), .Select("low")) register_27 (
    .D(Din), .en(decoder_1_out5), .Q(register_27_q), .clk(clk_out), .clr(clear), .cs(enable), .preset(preset));
  Register #(.width(32), .trigger("rising"), .Select("low")) register_28 (
    .D(Din), .en(decoder_1_out4), .Q(register_28_q), .clk(clk_out), .clr(clear), .cs(enable), .preset(preset));
  Register #(.width(32), .trigger("rising"), .Select("low")) register_29 (
    .D(Din), .en(decoder_1_out3), .Q(register_29_q), .clk(clk_out), .clr(clear), .cs(enable), .preset(preset));
  Register #(.width(32), .trigger("rising"), .Select("low")) register_30 (
    .D(Din), .en(decoder_1_out2), .Q(register_30_q), .clk(clk_out), .clr(clear), .cs(enable), .preset(preset));
  Register #(.width(32), .trigger("rising"), .Select("low")) register_31 (
    .D(Din), .en(decoder_1_out1), .Q(register_31_q), .clk(clk_out), .clr(clear), .cs(enable), .preset(preset));
  Register #(.width(32), .trigger("rising"), .Select("low")) register_32 (
    .D(Din), .en(decoder_1_out0), .Q(register_32_q), .clk(clk_out), .clr(clear), .cs(enable), .preset(preset));
  Multiplexer #(.select(5), .width(32), .disabled("Z"), .enable("false")) multiplexer_1 (
    .in0(register_32_q), .in1(register_31_q), .in2(register_30_q), .in3(register_29_q), .in4(register_28_q),
    .in5(register_27_q), .in6(register_26_q), .in7(register_25_q), .in8(register_24_q), .in9(register_23_q),
    .in10(register_22_q), .in11(register_21_q), .in12(register_20_q), .in13(register_19_q),
    .in14(register_18_q), .in15(register_17_q), .in16(register_16_q), .in17(register_15_q),
    .in18(register_14_q), .in19(register_13_q), .in20(register_12_q), .in21(register_11_q),
    .in22(register_10_q), .in23(register_9_q), .in24(register_8_q), .in25(register_7_q), .in26(register_6_q),
    .in27(register_5_q), .in28(register_4_q), .in29(register_3_q), .in30(register_2_q), .in31(register_1_q),
    .out(RD1), .sel(AddrRead1));
  Multiplexer #(.select(5), .width(32), .disabled("Z"), .enable("false")) multiplexer_2 (
    .in0(register_32_q), .in1(register_31_q), .in2(register_30_q), .in3(register_29_q), .in4(register_28_q),
    .in5(register_27_q), .in6(register_26_q), .in7(register_25_q), .in8(register_24_q), .in9(register_23_q),
    .in10(register_22_q), .in11(register_21_q), .in12(register_20_q), .in13(register_19_q),
    .in14(register_18_q), .in15(register_17_q), .in16(register_16_q), .in17(register_15_q),
    .in18(register_14_q), .in19(register_13_q), .in20(register_12_q), .in21(register_11_q),
    .in22(register_10_q), .in23(register_9_q), .in24(register_8_q), .in25(register_7_q), .in26(register_6_q),
    .in27(register_5_q), .in28(register_4_q), .in29(register_3_q), .in30(register_2_q), .in31(register_1_q),
    .out(RD2), .sel(AddrRead2));
endmodule
